# Fritzing sketch blink_led (saved by Fritzing 0.9.4)
breadboards: 1

parts:
  Raspberry_Pi_1 = Raspberry Pi 3 [part_number=RPI-3-V1.2]
  LED1 = smd LED [color="Blue (430nm)" package="0603 [SMD]"]
  R1 = Resistor [tolerance=±5% resistance=220 package="0402 [SMD]"]

nets:
  N1: Raspberry_Pi_1.3v3, R1.Pin_1
  N2: Raspberry_Pi_1.GND, LED1.cathode
  N3: LED1.anode, R1.Pin_0
